// Logisim project FINAL_PROJECT.circ as structural Verilog: 3 circuits, main circuit FINAL
module FINAL (
  input  en,
  input  in_2
);

  wire and_1_out, and_2_out, b0, b1, b2, b3, b4, b5, b6, c0, c1, c2, c3, c4, c5, c6, clk, clock_1_out, G1,
       G2, or_1_out, pedestrian_button_1_en, R1, R2, rst, Y1, Y2;
  wire [3:0] downcounter_template_1_cout, downcounter_v1_1_count;
  wire [7:0] HEX0, HEX1;
  wire [7:7] bin2hex1_1_p5, bin2hex1_1_p6;

  and and_1 (and_1_out, ~downcounter_v1_1_count[0], ~downcounter_v1_1_count[1], ~downcounter_v1_1_count[2], ~downcounter_v1_1_count[3]);  // AND_Gate
  and and_2 (and_2_out, en, and_1_out);
  Clock u_clk (.out(clk));
  Button u_rst ();  // open: out
  // RGBLED rgbled_1: pin names not known; wires that end beside it: R1
  // RGBLED rgbled_2: pin names not known; wires that end beside it: Y1, Y1
  // RGBLED rgbled_3: pin names not known; wires that end beside it: G1
  or or_1 (or_1_out, rst, pedestrian_button_1_en);
  FSM1 fsm1_1 (.en(en), .next_state(and_2_out), .G1(G1), .Y1(G2), .G2(Y1), .Y2(Y2), .rst(rst), .R1(R1), .R2(R2));
  // RGBLED rgbled_4: pin names not known; wires that end beside it: R2
  // RGBLED rgbled_5: pin names not known; wires that end beside it: Y2, Y2
  // RGBLED rgbled_6: pin names not known; wires that end beside it: G2
  DownCounter_v1 downcounter_v1_1 (.en(or_1_out), .clk(clk), .count(downcounter_v1_1_count));
  _7_Segment_Display #(.active("false")) u_7_segment_display_1 (
    .g(HEX1[6]), .f(HEX1[5]), .a(HEX1[0]), .b(HEX1[1]), .e(HEX1[4]), .d(HEX1[3]), .c(HEX1[2]), .dp(HEX1[7]));
  pedestrian_button pedestrian_button_1 (.counter(downcounter_v1_1_count), .en(pedestrian_button_1_en));
  _7_Segment_Display #(.active("false")) u_7_segment_display_2 (
    .g(HEX0[6]), .f(HEX0[5]), .a(HEX0[0]), .b(HEX0[1]), .e(HEX0[4]), .d(HEX0[3]), .c(HEX0[2]), .dp(HEX0[7]));
  Bin2Hex Bin2Hex_1 (
    .v3(downcounter_v1_1_count[3]), .v2(downcounter_v1_1_count[2]), .v1(downcounter_v1_1_count[1]),
    .v0(downcounter_v1_1_count[0]), .HEX1(HEX1), .HEX0(HEX0));
  Clock clock_1 (.out(clock_1_out));
  DownCounter_Template downcounter_template_1 (.en(in_2), .clk(clock_1_out), .cout(downcounter_template_1_cout));
  _7_Segment_Display #(.active("false")) L_7_Segment_Display_3 (
    .g(b6), .f(b5), .a(b0), .b(b1), .e(b4), .d(b3), .c(b2), .dp(1'b1));
  _7_Segment_Display #(.active("false")) L_7_Segment_Display_4 (
    .g(c6), .f(c5), .a(c0), .b(c1), .e(c4), .d(c3), .c(c2), .dp(1'b1));
  // Bin2Hex1 bin2hex1_1: pin names not known; wires that end beside it: downcounter_template_1_cout[3], downcounter_template_1_cout[2], downcounter_template_1_cout[1], downcounter_template_1_cout[0], {bin2hex1_1_p5[7], b6, b5, b4, b3, b2, b1, b0}, {bin2hex1_1_p6[7], c6, c5, c4, c3, c2, c1, c0}

  // Notes on the sheet:
  //   Traffic Light A
  //   Traffic Light B
  //   Counter Display
  //   Counter Display
endmodule

module FSM1 (
  input  en,
  input  next_state,
  output G1,
  output Y1,
  output G2,
  output Y2,
  output rst,
  output R1,
  output R2
);

  wire [0:0] register_1_q;
  wire [1:0] multiplexer_1_out;

  Multiplexer #(.select(3), .width(2)) multiplexer_1 (
    .in0(2'b00), .in1(2'b01), .in2(2'b10), .in3(2'b11), .in4(2'b01), .in5(2'b10), .in6(2'b11), .in7(2'b00),
    .out(multiplexer_1_out), .sel({en, R1, register_1_q[0]}));
  // Probe on multiplexer_1_out
  Register #(.width(2)) register_1 (
    .D(multiplexer_1_out), .Q({R1, register_1_q[0]}), .clk(next_state));  // open: en, clr
  // Probe on {R1, register_1_q[0]}
  and and_1 (G1, ~register_1_q[0], ~R1);  // AND_Gate
  and and_2 (Y1, ~register_1_q[0], R1);  // AND_Gate
  and and_3 (G2, register_1_q[0], ~R1);  // AND_Gate
  and and_4 (Y2, register_1_q[0], R1);
  not not_1 (R2, R1);

  assign rst = next_state;
endmodule

module FSM2 (
  input  en,
  input  next_state,
  output G,
  output Y,
  output R,
  output rst
);

  wire [1:0] multiplexer_1_out, register_1_q;

  Multiplexer #(.select(3), .width(2)) multiplexer_1 (
    .in0(2'b00), .in1(2'b01), .in2(2'b10), .in4(2'b01), .in5(2'b10), .in6(2'b00), .out(multiplexer_1_out),
    .sel({en, register_1_q}));  // open: in3, in7
  // Probe on multiplexer_1_out
  Register #(.width(2)) register_1 (.D(multiplexer_1_out), .Q(register_1_q), .clk(next_state));  // open: en, clr
  // Probe on register_1_q
  and and_1 (G, ~register_1_q[0], ~register_1_q[1]);  // AND_Gate
  and and_2 (Y, register_1_q[1], ~register_1_q[0]);  // AND_Gate
  and and_3 (R, ~register_1_q[1], register_1_q[0]);  // AND_Gate

  assign rst = next_state;
endmodule
