// Logisim project something.circ as structural Verilog: 4 circuits, main circuit main
module main (
  input  in_1,
  input  in_2,
  input  in_3,
  output out_4,
  output out_5
);

  HA ha_1 ();  // open: x, y, s, c
  FA fa_1 ();  // open: x, y, cin, z, cout
endmodule

module FA (
  input  x,
  input  y,
  input  cin,
  output z,
  output cout
);

  wire and_1_out, and_2_out, and_3_out, and_4_out, and_5_out, and_6_out, and_7_out, not_1_out, not_2_out,
       not_3_out;

  not not_1 (not_1_out, x);
  not not_2 (not_2_out, y);
  not not_3 (not_3_out, cin);
  and and_1 (and_1_out, not_1_out, not_2_out, cin);
  and and_2 (and_2_out, not_1_out, y, not_3_out);
  and and_3 (and_3_out, x, not_2_out, not_3_out);
  and and_4 (and_4_out, x, y, cin);
  and and_5 (and_5_out, y, cin);
  and and_6 (and_6_out, x, cin);
  and and_7 (and_7_out, x, y);
  or or_1 (z, and_1_out, and_2_out, and_3_out, and_4_out);
  or or_2 (cout, and_5_out, and_6_out, and_7_out);
endmodule

module HA (
  input  x,
  input  y,
  output s,
  output c
);

  wire and_1_out, and_2_out, not_1_out, not_2_out;

  not not_1 (not_1_out, x);
  not not_2 (not_2_out, y);
  and and_1 (and_1_out, not_1_out, y);
  and and_2 (and_2_out, x, not_2_out);
  and and_3 (c, x, y);
  or or_1 (s, and_1_out, and_2_out);
endmodule

module Ripple (
  input  [3:0] z,
  input  [3:0] x,
  input  [3:0] y,
  output cout
);

  wire fa_1_z, fa_2_z, fa_3_z, y3;

  FA fa_1 (.x(x[0]), .y(x[1]), .cin(1'b0), .z(fa_1_z), .cout(z[0]));
  FA fa_2 (.x(x[2]), .y(x[3]), .cin(fa_1_z), .z(fa_2_z), .cout(z[1]));
  FA fa_3 (.x(y[0]), .y(y[1]), .cin(fa_2_z), .z(fa_3_z), .cout(z[2]));
  FA fa_4 (.x(y3), .y(y[3]), .cin(fa_3_z), .z(cout), .cout(z[3]));

  // Other names for the same wires on the sheet: x1 = x[0]; x2 = x[1]; x3 = x[2]; x4 = x[3]; y1 = y[0]; y2 = y[1];
  //   y4 = y[3]; z1 = z[0]; z2 = z[1]; z3 = z[2]; z4 = z[3]
endmodule
