// Logisim project LAB8.circ as structural Verilog: 1 circuit, main circuit main
module main (
  input  Input_1,
  input  Input_2,
  input  Input_3,
  input  [1:0] input_bus_1,
  output R,
  output G,
  output B,
  output Output_1,
  output Output_2,
  output Output_3
);

  wire clock_1_out;
  wire [1:1] undriven;
  wire [2:0] register_1_q;

  Register #(.width(3)) register_1 (.Q(register_1_q), .clk(clock_1_out));  // open: D, en, clr
  Clock clock_1 (.out(clock_1_out));
  Clock clock_2 ();  // open: out
  Clock clock_3 ();  // open: out
  Clock clock_4 ();  // open: out
  Multiplexer #(.select(2), .width(3)) multiplexer_1 (
    .in0(register_1_q), .in1({1'b1, undriven[1], 1'b1}), .in2({register_1_q[1], 2'b11}),
    .out({Output_3, Output_2, Output_1}), .sel(input_bus_1));  // open: in3
endmodule
